// Digital circuit Punto3aFlipFlopRS.dig as structural Verilog
module Punto3aFlipFlopRS (
  input  S,
  input  R,
  input  Clock,
  output Q,
  output Q_2,
  output Q_3
);

  wire nand_1_out, nand_2_out;

  nand nand_1 (nand_1_out, S, Clock);
  nand nand_2 (nand_2_out, Clock, R);
  nand nand_3 (Q_2, nand_1_out, Q_3);
  nand nand_4 (Q_3, Q_2, nand_2_out);
  RS_FF rs_ff_1 (.S(S), .C(Clock), .R(R), .Q(Q));  // open: nQ

  // Notes on the sheet:
  //   Condiciones
  //   El funcionamiento viene dado cuando el clock esta activo permite
  //   cambiar los valores con S(1) y R(0), el problema se da cuando ambos 
  //   se activan (S y R) a la vez y el clock esta activo, por lo que nos quedan
  //   Q y Q' como 1, lo que genera que al quitar el Clock el circuito de una
  //   respuesta incierta, ya que empezara a oscilar dependiendo de cuál de 
  //   los dos NAND de la parte final cambie a 0 primero.
  //   El funcionamiento de una forma más detallada se puede obserrvar
  //   al analizar la retroalimentación que se da en las salidas Q y Q' en los NANDs finales
  //   que mantieneel valor constante a menos que los NANDs del comienzo digan lo contrario.
  //   Ya que una de las entradas de esos NANDs es el clock sin que este este activo es
  //   imposible cambiar el valor de Q y Q'.
  //   FlipFlopRS
  //   Circuito de referencia
endmodule
