// Digital circuit Punto3bFlipFlopJK.dig as structural Verilog
module Punto3bFlipFlopJK (
  input  J,
  input  K,
  input  Clock,
  output Q,
  output Q_2,
  output Q_3,
  output Q_4,
  output Q_5
);

  wire nand_1_out, nand_2_out, nand_5_out, nand_6_out, nand_7_out, nand_8_out, nand_9_out, nand_10_out,
       not_1_out;

  nand nand_1 (nand_1_out, J, Q_5, Clock);
  nand nand_2 (nand_2_out, Clock, Q_4, K);
  JK_FF jk_ff_1 (.J(J), .C(Clock), .K(K), .Q(Q));  // open: nQ
  nand nand_3 (Q_4, nand_1_out, Q_5);
  nand nand_4 (Q_5, Q_4, nand_2_out);
  nand nand_5 (nand_5_out, J, Q_3, Clock);
  nand nand_6 (nand_6_out, Clock, Q_2, K);
  nand nand_7 (nand_7_out, nand_5_out, nand_8_out);
  nand nand_8 (nand_8_out, nand_7_out, nand_6_out);
  not not_1 (not_1_out, Clock);
  nand nand_9 (nand_9_out, nand_7_out, not_1_out);
  nand nand_10 (nand_10_out, not_1_out, nand_8_out);
  nand nand_11 (Q_2, nand_9_out, Q_3);
  nand nand_12 (Q_3, Q_2, nand_10_out);

  // Notes on the sheet:
  //   Condiciones
  //   El cambio en Q viene dado cuando Clock
  //   se encuentra activo y alguna de las opciones
  //   J(1) y K(0) también, a diferencia del RS no permite
  //   tener en true  a la vez a Q y Q', pero al tener ambas
  //   opcines encendidas a la vez el circuito tiende a 
  //   oscilar de un valor al otro, por lo que la simulación 
  //   falla.
  //   A diferencia del RS, no me permite tener Q y Q' en 1
  //   simultaneamente ya que la retroalimentación que se hace
  //   de Q' y Q en los primeros NAND los hace totalmente 
  //   escluyenes, de resto funciona de una forma similar al RS
  //   FlipFlopJK
  //   Circuito de referencia
  //   FlipFlopJK Variante Con Master-Slave
  //   Esta variante nos permite con el mismo Flip Flop JK evitar
  //   los problemas de oscilaciones al tener un circuito maestro
  //   que es en el cuál se ponen las condiciones a "guardar" y otro
  //   esclavo que recibe las ordenes de su maestro despues de que el clock se apaga, 
  //   este retraso que se da ya que el master se actualiza
  //   cuando el clock esta encendido y el slave cuando esta apagado, nos quita
  //   el problema de las oscilaciones que se presentan en la variante normal
endmodule
